// Logisim project ADDERKAMALSBC.circ as structural Verilog
module GHTT (
  input  A,
  input  B,
  input  CIN,
  output SUM,
  output COUT
);

  wire and_1_out, and_2_out, and_3_out, and_4_out, and_5_out, and_6_out, and_7_out, not_1_out, not_2_out,
       not_3_out, not_4_out, not_5_out, not_6_out;

  not not_1 (not_1_out, A);
  not not_2 (not_2_out, B);
  not not_3 (not_3_out, A);
  not not_4 (not_4_out, CIN);
  not not_5 (not_5_out, B);
  not not_6 (not_6_out, CIN);
  and and_1 (and_1_out, B, CIN);
  and and_2 (and_2_out, A, CIN);
  and and_3 (and_3_out, A, B);
  and and_4 (and_4_out, not_1_out, not_2_out, CIN);
  and and_5 (and_5_out, not_3_out, B, not_4_out);
  and and_6 (and_6_out, A, not_5_out, not_6_out);
  and and_7 (and_7_out, A, B, CIN);
  or or_1 (COUT, and_1_out, and_2_out, and_3_out);
  or or_2 (SUM, and_4_out, and_5_out, and_6_out, and_7_out);
endmodule

module UFJFJFJF (
  input  A,
  input  B,
  input  CIN,
  output SUM,
  output COUT
);

  wire and_1_out, and_2_out, and_3_out, and_4_out, and_5_out, and_6_out, and_7_out, not_1_out, not_2_out,
       not_3_out, not_4_out, not_5_out, not_6_out;

  not not_1 (not_1_out, A);
  not not_2 (not_2_out, B);
  not not_3 (not_3_out, A);
  not not_4 (not_4_out, CIN);
  not not_5 (not_5_out, B);
  not not_6 (not_6_out, CIN);
  and and_1 (and_1_out, B, CIN);
  and and_2 (and_2_out, A, CIN);
  and and_3 (and_3_out, A, B);
  and and_4 (and_4_out, not_1_out, not_2_out, CIN);
  and and_5 (and_5_out, not_3_out, B, not_4_out);
  and and_6 (and_6_out, A, not_5_out, not_6_out);
  and and_7 (and_7_out, A, B, CIN);
  or or_1 (COUT, and_1_out, and_2_out, and_3_out);
  or or_2 (SUM, and_4_out, and_5_out, and_6_out, and_7_out);
endmodule

module JFJFJFJF (
  input  A,
  input  B,
  input  CIN,
  output SUM,
  output COUT
);

  wire nand_1_out, nand_2_out, nand_3_out, nand_4_out, nand_5_out, nand_6_out, nand_7_out, nand_8_out,
       nand_9_out, nand_10_out, nand_11_out, nand_12_out, nand_13_out, nand_14_out, nand_15_out, nand_16_out,
       nand_17_out, nand_18_out, nand_19_out, nand_20_out, nand_21_out, nand_22_out, nand_23_out,
       nand_25_out, nand_26_out, nand_27_out, nand_28_out;

  nand nand_1 (nand_1_out, A, A);
  nand nand_2 (nand_2_out, B, B);
  nand nand_3 (nand_3_out, A, A);
  nand nand_4 (nand_4_out, B, B);
  nand nand_5 (nand_5_out, B, CIN);
  nand nand_6 (nand_6_out, A, CIN);
  nand nand_7 (nand_7_out, nand_1_out, nand_2_out);
  nand nand_8 (nand_8_out, nand_3_out, B);
  nand nand_9 (nand_9_out, A, nand_4_out);
  nand nand_10 (nand_10_out, A, B);
  nand nand_11 (nand_11_out, nand_5_out, nand_6_out);
  nand nand_12 (nand_12_out, nand_7_out, nand_7_out);
  nand nand_13 (nand_13_out, nand_8_out, nand_8_out);
  nand nand_14 (nand_14_out, CIN, CIN);
  nand nand_15 (nand_15_out, nand_9_out, nand_9_out);
  nand nand_16 (nand_16_out, CIN, CIN);
  nand nand_17 (nand_17_out, nand_10_out, nand_10_out);
  nand nand_18 (nand_18_out, nand_11_out, nand_11_out);
  nand nand_19 (nand_19_out, A, B);
  nand nand_20 (nand_20_out, nand_12_out, CIN);
  nand nand_21 (nand_21_out, nand_13_out, nand_14_out);
  nand nand_22 (nand_22_out, nand_15_out, nand_16_out);
  nand nand_23 (nand_23_out, nand_17_out, CIN);
  nand nand_24 (COUT, nand_18_out, nand_19_out);
  nand nand_25 (nand_25_out, nand_20_out, nand_21_out);
  nand nand_26 (nand_26_out, nand_22_out, nand_23_out);
  nand nand_27 (nand_27_out, nand_25_out, nand_25_out);
  nand nand_28 (nand_28_out, nand_26_out, nand_26_out);
  nand nand_29 (SUM, nand_27_out, nand_28_out);
endmodule

module ADDDERRTT (
  input  A,
  input  B,
  input  CIN,
  output SUM,
  output COUT
);

  wire and_1_out, and_2_out, and_3_out, and_4_out, and_5_out, and_6_out, and_7_out, not_1_out, not_2_out,
       not_3_out, not_4_out, not_5_out, not_6_out;

  not not_1 (not_1_out, A);
  not not_2 (not_2_out, B);
  not not_3 (not_3_out, A);
  not not_4 (not_4_out, CIN);
  not not_5 (not_5_out, B);
  not not_6 (not_6_out, CIN);
  and and_1 (and_1_out, B, CIN);
  and and_2 (and_2_out, A, CIN);
  and and_3 (and_3_out, A, B);
  and and_4 (and_4_out, not_1_out, not_2_out, CIN);
  and and_5 (and_5_out, not_3_out, B, not_4_out);
  and and_6 (and_6_out, A, not_5_out, not_6_out);
  and and_7 (and_7_out, A, B, CIN);
  or or_1 (COUT, and_1_out, and_2_out, and_3_out);
  or or_2 (SUM, and_4_out, and_5_out, and_6_out, and_7_out);
endmodule

module JFJFJF (
  input  A,
  input  B,
  input  CIN,
  output SUM,
  output COUT
);

  wire and_1_out, and_2_out, and_3_out, not_1_out, not_2_out, not_3_out, not_4_out, not_5_out, not_6_out,
       or_1_out, or_2_out, or_3_out, or_4_out;

  not not_1 (not_1_out, B);
  not not_2 (not_2_out, CIN);
  not not_3 (not_3_out, A);
  not not_4 (not_4_out, CIN);
  not not_5 (not_5_out, A);
  not not_6 (not_6_out, B);
  and and_1 (and_1_out, B, CIN);
  and and_2 (and_2_out, A, CIN);
  and and_3 (and_3_out, A, B);
  or or_1 (or_1_out, A, B, CIN);
  or or_2 (or_2_out, A, not_1_out, not_2_out);
  or or_3 (or_3_out, not_3_out, B, not_4_out);
  or or_4 (or_4_out, not_5_out, not_6_out, CIN);
  or or_5 (COUT, and_1_out, and_2_out, and_3_out);
  and and_4 (SUM, or_1_out, or_2_out, or_3_out, or_4_out);
endmodule

module JYFDKYDYD (
  input  A,
  input  B,
  input  CIN,
  output SUM,
  output COUT
);

  wire and_1_out, and_2_out, and_3_out, not_1_out, not_2_out, not_3_out, not_4_out, not_5_out, not_6_out,
       or_1_out, or_2_out, or_3_out, or_4_out;

  not not_1 (not_1_out, B);
  not not_2 (not_2_out, CIN);
  not not_3 (not_3_out, A);
  not not_4 (not_4_out, CIN);
  not not_5 (not_5_out, A);
  not not_6 (not_6_out, B);
  and and_1 (and_1_out, B, CIN);
  and and_2 (and_2_out, A, CIN);
  and and_3 (and_3_out, A, B);
  or or_1 (or_1_out, A, B, CIN);
  or or_2 (or_2_out, A, not_1_out, not_2_out);
  or or_3 (or_3_out, not_3_out, B, not_4_out);
  or or_4 (or_4_out, not_5_out, not_6_out, CIN);
  or or_5 (COUT, and_1_out, and_2_out, and_3_out);
  and and_4 (SUM, or_1_out, or_2_out, or_3_out, or_4_out);
endmodule
