// Logisim project KAMALSBCDIVIDERR.circ as structural Verilog
module KAMALSBCDIVIDER (
  input  A,
  input  B,
  output Q,
  output R
);


  assign Q = A;
  assign R = 1'b0;
endmodule
